# Fritzing sketch onOffTestCircuit (saved by Fritzing 0.9.3b)
breadboards: 1

parts:
  Part1 = Arduino Uno (Rev3)
  R1 = Resistor [tolerance=±5% resistance=220 package=THT]
  LED1 = LED - 5mm [color="Red (633nm)" package="5 mm [THT]"]
  S1 = Pushbutton [package="[THT]"]

nets:
  N1: Part1.A0, R1.Pin_0, LED1.anode
  N2: Part1.A1, Part1.GND, S1.Pin_1, S1.Pin_2
  N3: Part1.5V, R1.Pin_1
  N4: LED1.cathode, S1.Pin_3, S1.Pin_4
